# Fritzing sketch AlarmClock (saved by Fritzing 0.9.3b)
circuit board: 10.6628cm x 5.05124cm
breadboards: 3

parts:
  U3 = 74HC595 [package="DIP16 [THT]"]
  U2 = 74HC595 [package="DIP16 [THT]"]
  U10 = DS3231 [part_number=DS3231 package=THT]
  U1 = atmega328 [package=dip]
  U9 = KY-040 Potentiometer w/ Switch [part_number=KY-040 package=THT]
  R1 = Resistor [tolerance=±5% resistance=10k package=THT]
  S1 = Pushbutton [package="[THT]"]
  U8 = KY-040 Potentiometer w/ Switch [part_number=KY-040 package=THT]
  U4 = 74HC595 [package="DIP16 [THT]"]
  C1 = Ceramic Capacitor [capacitance=1µF package="100 mil [THT, multilayer]"]
  R2 = Resistor [tolerance=±5% resistance=150 package=THT]
  R3 = Resistor [tolerance=±5% resistance=150 package=THT]
  R4 = Resistor [tolerance=±5% resistance=150 package=THT]
  R5 = Resistor [tolerance=±5% resistance=150 package=THT]
  R6 = Resistor [tolerance=±5% resistance=150 package=THT]
  R7 = Resistor [tolerance=±5% resistance=150 package=THT]
  R8 = Resistor [tolerance=±5% resistance=150 package=THT]
  R9 = Resistor [tolerance=±5% resistance=150 package=THT]
  R10 = Resistor [tolerance=±5% resistance=150 package=THT]
  R11 = Resistor [tolerance=±5% resistance=150 package=THT]
  R12 = Resistor [tolerance=±5% resistance=150 package=THT]
  R13 = Resistor [tolerance=±5% resistance=150 package=THT]
  R14 = Resistor [tolerance=±5% resistance=150 package=THT]
  R15 = Resistor [tolerance=±5% resistance=150 package=THT]
  R16 = Resistor [tolerance=±5% resistance=150 package=THT]
  R17 = Resistor [tolerance=±5% resistance=150 package=THT]
  R18 = Resistor [tolerance=±5% resistance=150 package=THT]
  R19 = Resistor [tolerance=±5% resistance=150 package=THT]
  R20 = Resistor [tolerance=±5% resistance=150 package=THT]
  R21 = Resistor [tolerance=±5% resistance=150 package=THT]
  R22 = Resistor [tolerance=±5% resistance=150 package=THT]
  R23 = Resistor [tolerance=±5% resistance=150 package=THT]
  R24 = Resistor [tolerance=±5% resistance=150 package=THT]
  R25 = Resistor [tolerance=±5% resistance=150 package=THT]
  J1 = Generic female header - 2 pins [form="♀ (female)" package=THT]
  J2 = Generic female header - 2 pins [form="♀ (female)" package=THT]
  J3 = Generic female header - 2 pins [form="♀ (female)" package=THT]
  J4 = Generic female header - 2 pins [form="♀ (female)" package=THT]
  J5 = Generic female header - 2 pins [form="♀ (female)" package=THT]
  J9 = Generic female header - 2 pins [form="♀ (female)" package=THT]
  J12 = Generic female header - 2 pins [form="♀ (female)" package=THT]
  J15 = Generic female header - 2 pins [form="♀ (female)" package=THT]
  J14 = Generic female header - 2 pins [form="♀ (female)" package=THT]
  J11 = Generic female header - 2 pins [form="♀ (female)" package=THT]
  J8 = Generic female header - 2 pins [form="♀ (female)" package=THT]
  J6 = Generic female header - 2 pins [form="♀ (female)" package=THT]
  J7 = Generic female header - 2 pins [form="♀ (female)" package=THT]
  J13 = Generic female header - 2 pins [form="♀ (female)" package=THT]
  J10 = Generic female header - 2 pins [form="♀ (female)" package=THT]
  J16 = Generic female header - 2 pins [form="♀ (female)" package=THT]
  J20 = Generic female header - 2 pins [form="♀ (female)" package=THT]
  J23 = Generic female header - 2 pins [form="♀ (female)" package=THT]
  J22 = Generic female header - 2 pins [form="♀ (female)" package=THT]
  J19 = Generic female header - 2 pins [form="♀ (female)" package=THT]
  J18 = Generic female header - 2 pins [form="♀ (female)" package=THT]
  J21 = Generic female header - 2 pins [form="♀ (female)" package=THT]
  J24 = Generic female header - 2 pins [form="♀ (female)" package=THT]
  J17 = Generic female header - 2 pins [form="♀ (female)" package=THT]
  part = Generic female header - 2 pins [form="♀ (female)" package=THT]
  R26 = Resistor [tolerance=±5% resistance=0 package=THT]
  C2 = Electrolytic Capacitor [capacitance=1µF package="100 mil [THT, electrolytic]"]
  C3 = Ceramic Capacitor [capacitance=1µF package="100 mil [THT, multilayer]"]
  R27 = Resistor [tolerance=±5% resistance=68 package=THT]
  J25 = Generic female header - 2 pins [form="♀ (female)" package=THT]
  J26 = Generic female header - 2 pins [form="♀ (female)" package=THT]
  part_2 = Generic female header - 2 pins [form="♀ (female)" package=THT]

nets:
  N1: U3.Q1, R12.Pin_0
  N2: U3.Q2, R16.Pin_0
  N3: U3.Q3, R13.Pin_0
  N4: U3.Q4, R15.Pin_0
  N5: U3.Q5, R17.Pin_0
  N6: U3.Q6, R11.Pin_0
  N7: U3.Q7, R14.Pin_0
  GND: U3.GND, U3.OE, U2.GND, U2.OE, U10.GND, U1.GND, U9.GND, S1.Pin_1, S1.Pin_2, U8.GND, U4.GND, U4.OE, C1.1, J1.GND, J2.GND, J3.GND, J4.GND, J5.GND, J9.GND, J12.GND, J15.GND, J14.GND, J11.GND, J8.GND, J6.GND, J7.GND, J13.GND, J10.GND, J16.GND, J20.GND, J23.GND, J22.GND, J19.GND, J18.GND, J21.GND, J24.GND, J17.GND, part.GND, C2.-, C3.1, J25.GND, J26.GND, part_2.GND
  N8: U3.Q7', U4.DS
  VCC: U3.MR, U3.VCC, U2.MR, U2.VCC, U10.VCC, U1.VCC, U1.AVCC, U9.VCC, R1.Pin_1, U8.VCC, U4.MR, U4.VCC, part.pin2, R26.Pin_1, C3.0
  N9: U3.SH_CP, U2.SH_CP, U1.D11_(PWM), U4.SH_CP
  N10: U3.ST_CP, U2.ST_CP, U1.D12, U4.ST_CP
  N11: U3.DS, U2.Q7'
  N12: U3.Q0, R10.Pin_0
  N13: U2.Q1, R3.Pin_0
  N14: U2.Q2, R4.Pin_0
  N15: U2.Q3, R5.Pin_0
  N16: U2.Q4, R6.Pin_0
  N17: U2.Q5, R7.Pin_0
  N18: U2.Q6, R8.Pin_0
  N19: U2.Q7, R9.Pin_0
  N20: U2.DS, U1.D10_(PWM)
  N21: U2.Q0, R2.Pin_0
  N22: U10.SCL, U1.A5
  N23: U10.SDA, U1.A4
  N24: U1.RESET, R1.Pin_0
  N25: U1.D0_(RX), U9.SW
  N26: U1.D1_(TX), S1.Pin_3, S1.Pin_4, R27.Pin_0
  N27: U1.D2, U8.CLK
  N28: U1.D3_(PWM), U8.DATA
  N29: U1.D4, U8.SW
  N30: U1.D6_(PWM), U9.CLK
  N31: U1.D7, U9.DATA
  N32: U1.A0, J26.pin2
  N33: U1.A1, part_2.pin2
  N34: U1.A3, J25.pin2
  N35: U4.Q1, R19.Pin_0
  N36: U4.Q2, R25.Pin_0
  N37: U4.Q3, R18.Pin_0
  N38: U4.Q4, R22.Pin_0
  N39: U4.Q5, R20.Pin_0
  N40: U4.Q6, R24.Pin_0
  N41: U4.Q7, R21.Pin_0
  N42: U4.Q0, R23.Pin_0
  N43: C1.0, R27.Pin_1
  N44: R2.Pin_1, J1.pin2
  N45: R3.Pin_1, J2.pin2
  N46: R4.Pin_1, J3.pin2
  N47: R5.Pin_1, J4.pin2
  N48: R6.Pin_1, J5.pin2
  N49: R7.Pin_1, J6.pin2
  N50: R8.Pin_1, J7.pin2
  N51: R9.Pin_1, J8.pin2
  N52: R10.Pin_1, J9.pin2
  N53: R11.Pin_1, J10.pin2
  N54: R12.Pin_1, J11.pin2
  N55: R13.Pin_1, J12.pin2
  N56: R14.Pin_1, J13.pin2
  N57: R15.Pin_1, J14.pin2
  N58: R16.Pin_1, J15.pin2
  N59: R17.Pin_1, J16.pin2
  N60: R18.Pin_1, J17.pin2
  N61: R19.Pin_1, J18.pin2
  N62: R20.Pin_1, J19.pin2
  N63: R21.Pin_1, J20.pin2
  N64: R22.Pin_1, J21.pin2
  N65: R23.Pin_1, J22.pin2
  N66: R24.Pin_1, J23.pin2
  N67: R25.Pin_1, J24.pin2
  N68: R26.Pin_0, C2.+

notes:
  GND
  VCC
  SDA
  SCL
  SQW
  32K
  SW
  DAT
  CLK
  VIN
  -
  www.edmoss.me
  A3|A1|A0

custom parts:
  DS3231: The DS3231 is a low-cost, extremely accurate I²C real-time clock (RTC) with an integrated temperature-compensated crystal oscillator (TCXO) and crystal. The device incorporates a battery input, and maintains accurate timekeeping when main power to the device is interrupted. The integration of the crystal resonator enhances the long-term accuracy of the device as well as reduces the piece-part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
  KY-040 Potentiometer w/ Switch: A 5 pin potentiometer with included switch. Intended for PCB Via Holes.
  Generic female header - 2 pins: Generic female header
